# Fritzing sketch board-v2 (saved by Fritzing 1.0.7)
circuit board: 7.88978cm x 4.98515cm
stripboards: 1

parts:
  L_sens_SL_N = Camdenboss CTB0158-3 [part_number=CTB0158-3 package=THT]
  L_in_N = Camdenboss CTB0158-2 [part_number=CTB0158-2 package=THT]
  J1 = Camdenboss CTB0158-6 [part_number=CTB0158-6 package=THT]
  F1 = FUSE [package=fuse_5mm]
  L_out_N = Camdenboss CTB0158-2 [part_number=CTB0158-2 package=THT]
  U1 = 888H-1CC-F-C E [part_number="888H-1CC-F-C E"]
  D1 = LED - 5mm [color="Red (633nm)" current=0.030A package="5 mm [THT]"]
  R2 = Resistor [tolerance=±5% power=2W resistance=15k package=THT]
  R1 = Resistor [tolerance=±5% power=2W resistance=15k package=THT]
  D5 = Rectifier Diode [part_number=1N4007 package="300 mil [THT]"]
  D3 = LED - 5mm [color="Red (633nm)" current=0.030A package="5 mm [THT]"]
  D4 = Rectifier Diode [part_number=1N4001 package="300 mil [THT]"]
  D2 = Rectifier Diode [part_number=1N4001 package="300 mil [THT]"]

nets:
  N1: L_sens_SL_N.pin1, J1.pin4, J1.pin5, J1.terminal_4, F1.2, U1.9_COM, U1.14_COM, R1.Pin_1
  N2: L_sens_SL_N.pin2, U1.22_-
  N3: L_sens_SL_N.pin3, L_in_N.pin2, J1.pin1, J1.pin2, L_out_N.pin2, U1.1_+, D5.cathode
  N4: L_in_N.pin1, F1.1
  N5: J1.pin3, L_out_N.pin1
  N6: J1.pin6, U1.11_N.O., U1.12_N.O., R2.Pin_1
  N7: D1.cathode, D5.anode, D3.cathode, D4.anode, D2.anode
  N8: D1.anode, R1.Pin_0, D2.cathode
  N9: R2.Pin_0, D3.anode, D4.cathode

notes:
  SLIP 2.0
